# Fritzing sketch espalti (saved by Fritzing 0.9.3b)
circuit board: 6.25968cm x 2.64651cm
breadboards: 1

parts:
  J1 = female pin header, 2 pins [form="♀ (female)"]
  J2 = female pin header, 2 pins [form="♀ (female)"]
  J4 = female pin header, 2 pins [form="♀ (female)"]
  J5 = female pin header, 2 pins [form="♀ (female)"]
  Part1 = Adafruit HUZZAH32 ESP32 Feather [part_number="Adafruit #3405"]

nets:
  N1: J1.pin1, J5.pin2, Part1.3.3V
  N2: J1.pin2, J4.pin1, Part1.GND
  N3: J2.pin1, Part1.SCL
  N4: J2.pin2, Part1.SDA
  N5: J4.pin2, J5.pin1, Part1.A4_IO36
